# Fritzing sketch codigo-morse-protoboard (saved by Fritzing 0.9.3b)
breadboards: 1

parts:
  Componente2 = Arduino Uno (Rev3)
  LED6 = LED - 5mm [color="Red (633nm)" package="5 mm [THT]"]
  R6 = Resistor [tolerance=±5% resistance=220 package=THT]

nets:
  N1: Componente2.D2, LED6.cathode
  N2: Componente2.GND, R6.Pin_1
  N3: LED6.anode, R6.Pin_0
